# Fritzing sketch VigiaSeniorV2_esquema (saved by Fritzing 1.0.6)
breadboards: 1

parts:
  Nano1 = Arduino Nano v2.3
  LED1 = smd LED [color="Blue (430nm)" package="1206 [SMD]"]
  LED2 = smd LED [color="Green (560nm)" package="1206 [SMD]"]
  LED3 = smd LED [color="Yellow (585nm)" package="1206 [SMD]"]
  LED4 = smd LED [color="Orange (605nm)" package="1206 [SMD]"]
  LED5 = smd LED [color="Red (633nm)" package="1206 [SMD]"]
  LED6 = smd LED [color="White (8000K)" package="1206 [SMD]"]
  R3 = Resistor [tolerance=±5% power=0.25W resistance=220 package=THT]
  R4 = Resistor [tolerance=±5% power=0.25W resistance=220 package=THT]
  R5 = Resistor [tolerance=±5% power=0.25W resistance=220 package=THT]
  R6 = Resistor [tolerance=±5% power=0.25W resistance=220 package=THT]
  R7 = Resistor [tolerance=±5% power=0.25W resistance=220 package=THT]
  R8 = Resistor [tolerance=±5% power=0.25W resistance=220 package=THT]
  S1 = Pushbutton [package="[THT]"]
  S2 = Pushbutton [package="[THT]"]
  S3 = Pushbutton [package="[THT]"]
  S4 = Pushbutton [package="[THT]"]
  S5 = Pushbutton [package="[THT]"]
  S6 = Pushbutton [package="[THT]"]
  S7 = Pushbutton [package="[THT]"]
  J1 = Piezo Speaker
  Q1 = PNP-Transistor [package="SOT-23 [SMD]"]
  R9_Base_1kΩ = Resistor [tolerance=±5% power=0.25W resistance=1000 package=THT]

nets:
  N1: Nano1.D3, Nano1.D4, Nano1.D5, Nano1.D6, Nano1.D7, Nano1.D8, Nano1.A6, Nano1.GND, S1.Pin_3, S1.Pin_4, S2.Pin_3, S2.Pin_4, S3.Pin_3, S3.Pin_4, S4.Pin_3, S4.Pin_4, S5.Pin_3, S5.Pin_4, S6.Pin_3, S6.Pin_4, S7.Pin_3, S7.Pin_4, J1.pin2
  N2: Nano1.D9, R9_Base_1kΩ.Pin_0
  N3: Nano1.3V3, LED1.cathode, LED2.cathode, LED3.cathode, LED4.cathode, LED5.cathode, LED6.cathode, Q1.0
  N4: Nano1.A5, R3.Pin_1
  N5: Nano1.A4, R8.Pin_1
  N6: Nano1.A3, R6.Pin_1
  N7: Nano1.A2, R7.Pin_1
  N8: Nano1.A1, R5.Pin_1
  N9: Nano1.A0, R4.Pin_1
  N10: LED1.anode, R3.Pin_0
  N11: LED2.anode, R8.Pin_0
  N12: LED3.anode, R6.Pin_0
  N13: LED4.anode, R7.Pin_0
  N14: LED5.anode, R5.Pin_0
  N15: LED6.anode, R4.Pin_0
  N16: J1.pin1, Q1.1
  N17: Q1.2, R9_Base_1kΩ.Pin_1
